# Fritzing sketch 接線圖 (saved by Fritzing 0.9.3b)
breadboards: 1

parts:
  元件1 = Arduino Mega 2560 (Rev3)
  L298N1 = L298N DC motor driver  # not connected
  M1 = Getriebemotor  # not connected
  A1 = HC-SR04 Ultrasonic Distance Sensor
  VCC1 = Battery  # not connected
  L298N2 = L298N DC motor driver  # not connected
  M2 = Getriebemotor  # not connected
  M3 = Getriebemotor  # not connected
  M4 = Getriebemotor  # not connected

nets:
  N1: 元件1.D30, A1.TRIG
  N2: 元件1.D31, A1.ECHO

custom parts:
  L298N DC motor driver: 2x DC motor driver with 78M05 positive voltage regulator (7..35 V) L298N: max 46 V, 2 A Set 5 V Enable jumper to enable 5 V regultor (needed for the L298N) and +5 V output at screw terminal or supply external +5 V at screw terminal Set ENA and/or ENB to +5 V to enable motor permanently or supply ENA and/or ENB with PWM signal IN1 and IN2 set rotation directory for motor A (OUT1/OUT2) IN2 and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
  HC-SR04 Ultrasonic Distance Sensor: The HC-SR04 is an ultrasonic distance sensor. It is capable of providing measurement for ranges of 2cm to 400cm. The module operates at 5V.
  Battery: Your standard 2x 18650 battery pack (7,4 Volts)
